// Logisim project Practica3.circ as structural Verilog
module Ejercicio9_1 (
  input  Antecedente,
  input  Consecuente,
  output Salida
);

  wire pull_resistor_2_node, transistor_1_out;

  Transistor transistor_1 (.in(1'b1), .out(transistor_1_out), .gate(Antecedente));
  Pull_Resistor pull_resistor_1 (.node(transistor_1_out));
  Pull_Resistor pull_resistor_2 (.node(pull_resistor_2_node));
  Transistor transistor_2 (.in(Antecedente), .out(pull_resistor_2_node), .gate(Consecuente));
  Transistor #(.\type ("n")) transistor_3 (.in(1'b1), .out(Salida), .gate(transistor_1_out));
  Transistor transistor_4 (.in(1'b1), .out(Salida), .gate(pull_resistor_2_node));
endmodule

module PersonalXOR (
  input  X,
  input  Y,
  output S
);

  wire and_1_out, and_2_out, not_1_out, not_2_out;

  not not_1 (not_1_out, X);
  not not_2 (not_2_out, Y);
  and and_1 (and_1_out, not_1_out, Y);
  and and_2 (and_2_out, X, not_2_out);
  or or_1 (S, and_1_out, and_2_out);
endmodule

module Ejercicio9_2 (
  input  [1:0] X,
  input  [1:0] Y,
  output Xmayor,
  output Igual,
  output Ymayor
);

  wire and_1_out, and_2_out, and_3_out, and_4_out, and_5_out, and_6_out, and_7_out, and_8_out, and_9_out,
       and_10_out, not_1_out, not_2_out, not_3_out, not_4_out;

  not not_1 (not_1_out, X[1]);
  not not_2 (not_2_out, X[0]);
  not not_3 (not_3_out, Y[1]);
  not not_4 (not_4_out, Y[0]);
  and and_1 (and_1_out, not_4_out, not_3_out, X[1]);
  and and_2 (and_2_out, X[0], X[1], not_3_out);
  and and_3 (and_3_out, not_4_out, X[0]);
  and and_4 (and_4_out, not_2_out, not_4_out, Y[1], X[1]);
  and and_5 (and_5_out, Y[0], X[0], not_3_out, not_1_out);
  and and_6 (and_6_out, Y[0], Y[1], not_1_out);
  and and_7 (and_7_out, Y[1], not_2_out, not_1_out);
  and and_8 (and_8_out, Y[0], not_2_out);
  or or_1 (Xmayor, and_1_out, and_2_out, and_3_out);
  and and_9 (and_9_out, not_4_out, not_3_out, not_2_out, not_1_out);
  or or_2 (Igual, and_9_out, and_4_out, and_5_out, and_10_out);
  and and_10 (and_10_out, Y[0], Y[1], X[0], X[1]);
  or or_3 (Ymayor, and_6_out, and_7_out, and_8_out);
endmodule
