// Logisim project Practica4.circ as structural Verilog
module Semisumador1Bit (
  input  X,
  input  Y,
  input  C,
  output Res,
  output Acarreo
);

  wire and_1_out, and_2_out, xor_1_out;

  xor xor_1 (xor_1_out, X, Y);
  and and_1 (and_1_out, xor_1_out, C);
  and and_2 (and_2_out, Y, X);
  xor xor_2 (Res, xor_1_out, C);
  or or_1 (Acarreo, and_1_out, and_2_out);
endmodule

module Semisumador8bits (
  input  [7:0] X,
  input  [7:0] Y,
  output [7:0] Salida,
  output Overflow
);

  wire _1_acarreo, _2_acarreo, _3_acarreo, _4_acarreo, _6_acarreo, semisumador1bit_1_acarreo,
       semisumador1bit_3_acarreo;

  Semisumador1Bit semisumador1bit_1 (
    .X(X[0]), .Y(Y[0]), .C(1'b0), .Res(Salida[0]), .Acarreo(semisumador1bit_1_acarreo));
  Semisumador1Bit _2 (.X(X[2]), .Y(Y[2]), .C(_1_acarreo), .Res(Salida[2]), .Acarreo(_2_acarreo));
  Semisumador1Bit _4 (.X(X[4]), .Y(Y[4]), .C(_3_acarreo), .Res(Salida[4]), .Acarreo(_4_acarreo));
  Semisumador1Bit _6 (.X(X[6]), .Y(Y[6]), .C(semisumador1bit_3_acarreo), .Res(Salida[6]), .Acarreo(_6_acarreo));
  Semisumador1Bit semisumador1bit_2 (.X(X[7]), .Y(Y[7]), .C(_6_acarreo), .Res(Salida[7]), .Acarreo(Overflow));
  Semisumador1Bit _1 (.X(X[1]), .Y(Y[1]), .C(semisumador1bit_1_acarreo), .Res(Salida[1]), .Acarreo(_1_acarreo));
  Semisumador1Bit _3 (.X(X[3]), .Y(Y[3]), .C(_2_acarreo), .Res(Salida[3]), .Acarreo(_3_acarreo));
  Semisumador1Bit semisumador1bit_3 (
    .X(X[5]), .Y(Y[5]), .C(_4_acarreo), .Res(Salida[5]), .Acarreo(semisumador1bit_3_acarreo));

  // Notes on the sheet:
  //   0
  //   0
  //   5
  //   7
endmodule

module \Sustracción  (
  input  [7:0] X,
  input  [7:0] Y,
  output [7:0] Resultado,
  output out_4
);

  wire [7:0] complementoa2_1_complementoa2;

  ComplementoA2 complementoa2_1 (.Entrada(Y), .ComplementoA2(complementoa2_1_complementoa2));  // open: Overflow
  Semisumador8bits semisumador8bits_1 (.X(X), .Y(complementoa2_1_complementoa2), .Salida(Resultado), .Overflow(out_4));

  // Notes on the sheet:
  //   ComplementoA2
  //   Sumador8bits
endmodule

module ComplementoA2 (
  input  [7:0] Entrada,
  output [7:0] ComplementoA2,
  output Overflow
);

  wire [7:0] not_1_out;

  not not_1 (not_1_out[0], Entrada[0]);
  not not_2 (not_1_out[1], Entrada[1]);
  not not_3 (not_1_out[2], Entrada[2]);
  not not_4 (not_1_out[3], Entrada[3]);
  not not_5 (not_1_out[4], Entrada[4]);
  not not_6 (not_1_out[5], Entrada[5]);
  not not_7 (not_1_out[6], Entrada[6]);
  not not_8 (not_1_out[7], Entrada[7]);
  Semisumador8bits semisumador8bits_1 (.X(not_1_out), .Y(8'h1), .Salida(ComplementoA2), .Overflow(Overflow));
endmodule

module SumadorYRestador (
  input  [7:0] X,
  input  [7:0] Y,
  input  \Selección ,
  output [7:0] Resultado
);

  wire [7:0] semisumador8bits_1_salida, \sustracción_1_resultado ;

  Semisumador8bits semisumador8bits_1 (.X(X), .Y(Y), .Salida(semisumador8bits_1_salida));  // open: Overflow
  \Sustracción  \sustracción_1  (.X(X), .Y(Y), .Resultado(\sustracción_1_resultado ));  // open: out_4
  Multiplexer #(.width(8)) multiplexer_1 (
    .in0(semisumador8bits_1_salida), .in1(\sustracción_1_resultado ), .out(Resultado), .sel(\Selección ),
    .en(1'b1));

  // Notes on the sheet:
  //   Sumador8
  //   Sustracción8
  //   Habilitador
endmodule
