// Logisim project Tarea04-circuitos.circ as structural Verilog: 15 circuits, main circuit main
module main (
  input  r,
  input  g,
  input  e,
  output G_2,
  output R_2
);

  wire and_1_out, and_2_out, not_1_out, not_2_out;

  not not_1 (not_1_out, g);
  not not_2 (not_2_out, e);
  and and_1 (and_1_out, r, not_1_out, e);
  and and_2 (and_2_out, r, g, not_2_out);
  and and_3 (G_2, g, e);
  or or_1 (R_2, and_1_out, and_2_out);

  // Notes on the sheet:
  //   Semaforo
endmodule

module _1_a (
  input  p,
  input  q,
  output out_3
);

  wire not_1_out, not_2_out;

  not not_1 (not_1_out, p);
  not not_2 (not_2_out, q);
  or or_1 (out_3, not_1_out, not_2_out);
endmodule

module _1_b (
  input  p,
  input  q,
  output S
);


  assign S = 1'b1;
endmodule

module _1_c (
  input  p,
  input  q,
  input  r,
  output S
);

  wire not_1_out;

  not not_1 (not_1_out, r);
  or or_1 (S, not_1_out, q);
endmodule

module _1_d (
  input  p,
  input  q,
  input  r,
  output S
);


  assign S = 1'b1;
endmodule

module NAND_circuits (
  input  Y,
  input  X,
  input  X_2,
  input  Y_2,
  input  X_3,
  output S,
  output out_7,
  output out_8
);

  wire nand_1_out, nand_2_out, nand_3_out, nand_4_out;

  nand nand_1 (nand_1_out, Y, Y);
  nand nand_2 (nand_2_out, X, X);
  nand nand_3 (nand_3_out, Y_2, X_3);
  nand nand_4 (nand_4_out, Y_2, X_3);
  nand nand_5 (S, nand_1_out, nand_2_out);
  nand nand_6 (out_8, nand_3_out, nand_4_out);
  nand nand_7 (out_7, X_2, X_2);

  // Notes on the sheet:
  //   OR
  //   AND
  //   NOT
endmodule

module Semisumador_1bit (
  input  X,
  input  Y,
  input  C,
  output Resultado,
  output Acarreo
);

  wire and_1_out, and_2_out, xor_1_out;

  xor xor_1 (xor_1_out, X, Y);
  and and_1 (and_1_out, X, Y);
  xor xor_2 (Resultado, xor_1_out, C);
  and and_2 (and_2_out, xor_1_out, C);
  or or_1 (Acarreo, and_2_out, and_1_out);
endmodule

module Semisumado_4bits (
  input  [3:0] X,
  input  [3:0] Y,
  output [3:0] Salida,
  output Acarreo
);

  wire semisumador_1bit_1_acarreo, semisumador_1bit_2_acarreo, semisumador_1bit_3_acarreo;

  Semisumador_1bit semisumador_1bit_1 (
    .X(X[0]), .Y(Y[0]), .C(1'b0), .Resultado(Salida[0]), .Acarreo(semisumador_1bit_1_acarreo));
  Semisumador_1bit semisumador_1bit_2 (
    .X(X[2]), .Y(Y[2]), .C(semisumador_1bit_3_acarreo), .Resultado(Salida[2]),
    .Acarreo(semisumador_1bit_2_acarreo));
  Semisumador_1bit semisumador_1bit_3 (
    .X(X[1]), .Y(Y[1]), .C(semisumador_1bit_1_acarreo), .Resultado(Salida[1]),
    .Acarreo(semisumador_1bit_3_acarreo));
  Semisumador_1bit semisumador_1bit_4 (
    .X(X[3]), .Y(Y[3]), .C(semisumador_1bit_2_acarreo), .Resultado(Salida[3]), .Acarreo(Acarreo));
endmodule

module _10_Mult (
  input  [3:0] Z,
  input  [3:0] Y,
  output [3:0] X,
  output Acarreo,
  output Overflow
);

  // Semisumado_4bits semisumado_4bits_1: pin names not known; wires that end beside it: Z, 1'b0, Y[0], Y[1], Y[2], X, Acarreo

  assign Overflow = Y[3];

  // Notes on the sheet:
  //   X=2Y+Z
endmodule

module Circ4_Motor (
  input  A,
  input  N,
  input  T,
  output Motor,
  output Lampara
);

  wire and_1_out, and_2_out, and_3_out, not_1_out, not_2_out, not_3_out, or_1_out;

  not not_1 (not_1_out, A);
  not not_2 (not_2_out, T);
  and and_1 (and_1_out, not_1_out, N);
  not not_3 (not_3_out, N);
  and and_2 (and_2_out, A, N);
  or or_1 (or_1_out, not_2_out, and_1_out);
  and and_3 (and_3_out, A, not_3_out);
  or or_2 (Lampara, T, and_2_out);
  or or_3 (Motor, or_1_out, and_3_out);
endmodule

module Circ4_Lampara (
  input  A,
  input  N,
  input  T,
  output Lampara
);

  wire and_1_out;

  and and_1 (and_1_out, A, N);
  or or_1 (Lampara, T, and_1_out);
endmodule

module Circ5_a (
  input  X0,
  input  X1,
  input  X2,
  output S
);

  wire and_1_out, and_2_out, not_1_out, not_2_out;

  not not_1 (not_1_out, X0);
  not not_2 (not_2_out, X1);
  and and_1 (and_1_out, X0, X1);
  and and_2 (and_2_out, not_1_out, not_2_out);
  or or_1 (S, and_1_out, and_2_out);

  // Notes on the sheet:
  //   Circ5-1
endmodule

module Circ5_b (
  input  x0,
  input  x1,
  input  x2,
  input  x3,
  output s
);

  wire and_1_out, and_2_out, and_3_out, not_1_out, not_2_out, not_3_out, not_4_out;

  not not_1 (not_1_out, x0);
  not not_2 (not_2_out, x1);
  not not_3 (not_3_out, x2);
  not not_4 (not_4_out, x3);
  and and_1 (and_1_out, not_1_out, not_2_out, not_3_out);
  and and_2 (and_2_out, not_1_out, not_2_out, not_4_out);
  and and_3 (and_3_out, x0, x1, not_4_out);
  or or_1 (s, and_1_out, and_2_out, and_3_out);

  // Notes on the sheet:
  //   Circuito 5 - 2
endmodule

module Circ5_c (
  input  x0,
  input  x1,
  input  x2,
  input  x3,
  input  x4,
  output s
);

  wire and_1_out, and_2_out, and_3_out, and_4_out, not_1_out, not_2_out, not_3_out, not_4_out, not_5_out,
       not_6_out, not_7_out, not_8_out, not_9_out, not_10_out;

  not not_1 (not_1_out, x0);
  not not_2 (not_2_out, x1);
  not not_3 (not_3_out, x2);
  not not_4 (not_4_out, x3);
  not not_5 (not_5_out, x4);
  not not_6 (not_6_out, x0);
  not not_7 (not_7_out, x1);
  not not_8 (not_8_out, x4);
  not not_9 (not_9_out, x2);
  not not_10 (not_10_out, x3);
  and and_1 (and_1_out, not_1_out, not_2_out, not_3_out, not_4_out, not_5_out);
  and and_2 (and_2_out, not_6_out, not_7_out, x2, x3, not_8_out);
  and and_3 (and_3_out, x1, not_9_out, not_10_out, x4);
  and and_4 (and_4_out, x0, x2, x3, x4);
  or or_1 (s, and_1_out, and_2_out, and_3_out, and_4_out);

  // Notes on the sheet:
  //   Circuito 5 - 3
endmodule

module Circ8_multi (
  input  [3:0] A,
  input  [3:0] B,
  output [7:0] out_3
);

  wire [2:0] and_6_out;
  wire [3:0] and_1_out, and_9_out, and_13_out, semisumado_4bits_2_salida;
  wire [3:1] semisumado_4bits_1_salida;
  wire [3:3] semisumado_4bits_1_acarreo;

  and and_1 (and_1_out[0], A[0], B[3]);
  and and_2 (and_1_out[1], A[1], B[3]);
  and and_3 (and_1_out[2], A[2], B[3]);
  and and_4 (and_1_out[3], A[3], B[3]);
  and and_5 (out_3[0], A[0], B[0]);
  and and_6 (and_6_out[0], A[1], B[0]);
  and and_7 (and_6_out[1], A[2], B[0]);
  and and_8 (and_6_out[2], A[3], B[0]);
  and and_9 (and_9_out[0], A[0], B[1]);
  and and_10 (and_9_out[1], A[1], B[1]);
  and and_11 (and_9_out[2], A[2], B[1]);
  and and_12 (and_9_out[3], A[3], B[1]);
  Semisumado_4bits semisumado_4bits_1 (
    .X({1'b0, and_6_out}), .Salida({semisumado_4bits_1_salida, out_3[1]}),
    .Acarreo(semisumado_4bits_1_acarreo[3]), .Y(and_9_out));
  and and_13 (and_13_out[0], A[0], B[2]);
  and and_14 (and_13_out[1], A[1], B[2]);
  and and_15 (and_13_out[2], A[2], B[2]);
  and and_16 (and_13_out[3], A[3], B[2]);
  Semisumado_4bits semisumado_4bits_2 (
    .X({semisumado_4bits_1_acarreo[3], semisumado_4bits_1_salida}),
    .Salida({semisumado_4bits_2_salida[2:0], out_3[2]}), .Acarreo(semisumado_4bits_2_salida[3]),
    .Y(and_13_out));
  Semisumado_4bits semisumado_4bits_3 (
    .X(semisumado_4bits_2_salida), .Salida(out_3[6:3]), .Acarreo(out_3[7]), .Y(and_1_out));

  // Notes on the sheet:
  //   Multiplicacion de 4 bits
endmodule
